# Fritzing sketch platine (saved by Fritzing 0.9.3b)
stripboards: 1

parts:
  J4 = male pin header, 2 pins [form="♂ (male)"]
  U1 = NodeMCU V1.0
  J7 = male pin header, 8 pins [form="♂ (male)"]
  DFPlayer_Mini1 = DFPlayer MINI [package="DIP (Dual Inline) [THT]"]
  J3 = screw terminal, 2 pins
  J8 = male pin header, 2 pins [form="♂ (male)"]
  R1 = Resistor [tolerance=±5% resistance=50 package=THT]

nets:
  N1: J4.pin1, J7.pin3
  N2: J4.pin2, DFPlayer_Mini1.SPK2, R1.Pin_0
  N3: U1.D1, DFPlayer_Mini1.TX
  N4: U1.D2, DFPlayer_Mini1.RX
  N5: U1.GND, DFPlayer_Mini1.GND#9
  N6: U1.RX, J7.pin6, J3.pin1, J3.pin2
  VIN: U1.Vin, J7.pin2, J7.pin7, DFPlayer_Mini1.VCC
  N7: U1.CLK, J8.pin1
  N8: U1.SD0, J7.pin1
  N9: U1.SD1, J7.pin8
  N10: J7.pin5, DFPlayer_Mini1.BUSY
  N11: DFPlayer_Mini1.IO_2, J8.pin2

custom parts:
  NodeMCU V1.0: ESP8266 based NodeMCU
  DFPlayer MINI: MP3 module by DFRobot.com for playing Music from an SD-Card. Supports WAV and MP3 files.
